# Fritzing sketch quizboard (saved by Fritzing 0.7.12b)
breadboards: 1

parts:
  DC_Power1 = DC Power [voltage=5]
  Arduino1 = Arduino
  R7 = Resistor [tolerance=±5% resistance=10k package=THT]
  R8 = Resistor [tolerance=±5% resistance=10k package=THT]
  R9 = Resistor [tolerance=±5% resistance=10k package=THT]
  P1 = S1133 Si Photodiode [package="8mm Ceramic [THT]"]
  P2 = S1133 Si Photodiode [package="8mm Ceramic [THT]"]
  P3 = S1133 Si Photodiode [package="8mm Ceramic [THT]"]
  S2 = Pushbutton [package=THT]
  S3 = Pushbutton [package=THT]
  S4 = Pushbutton [package=THT]
  S5 = Pushbutton [package=THT]
  S6 = Pushbutton [package=THT]
  R10 = Resistor [tolerance=±5% resistance=220 package=THT]
  R11 = Resistor [tolerance=±5% resistance=220 package=THT]
  R12 = Resistor [tolerance=±5% resistance=220 package=THT]
  R13 = Resistor [tolerance=±5% resistance=220 package=THT]
  R14 = Resistor [tolerance=±5% resistance=220 package=THT]
  LED4 = LED - 5mm [color="Red (633nm)" package="5 mm [THT]"]
  LED5 = LED - 5mm [color="Red (633nm)" package="5 mm [THT]"]
  Q1 = NPN-Transistor [package="TO92 [THT]"]
  R19 = Resistor [tolerance=±5% resistance=2.2k package=THT]
  LED7 = LED - 5mm [color="Red (633nm)" package="5 mm [THT]"]
  R21 = Resistor [tolerance=±5% resistance=470 package=THT]
  Q2 = NPN-Transistor [package="TO92 [THT]"]
  R22 = Resistor [tolerance=±5% resistance=2.2k package=THT]
  LED11 = LED - 5mm [color="Green (570nm)" package="5 mm [THT]"]
  LED12 = LED - 5mm [color="Green (570nm)" package="5 mm [THT]"]
  LED13 = LED - 5mm [color="Green (570nm)" package="5 mm [THT]"]
  R23 = Resistor [tolerance=±5% resistance=22 package=THT]
  Q3 = NPN-Transistor [package="TO92 [THT]"]
  R24 = Resistor [tolerance=±5% resistance=2.2k package=THT]
  SPKR2 = Loudspeaker
  R25 = Resistor [tolerance=±5% resistance=22 package=THT]
  LED15 = LED - 5mm [color="Red (633nm)" package="5 mm [THT]"]
  LED16 = LED - 5mm [color="Red (633nm)" package="5 mm [THT]"]
  LED17 = LED - 5mm [color="Red (633nm)" package="5 mm [THT]"]
  LED18 = LED - 5mm [color="Green (570nm)" package="5 mm [THT]"]
  LED19 = LED - 5mm [color="Red (633nm)" package="5 mm [THT]"]
  R26 = Resistor [tolerance=±5% resistance=470 package=THT]

nets:
  N1: DC_Power1.V+, Arduino1.+5V, R7.Pin_0, R8.Pin_0, R9.Pin_0, S2.leg0, S3.leg0, S4.leg0, S5.leg0, S6.leg0, LED4.anode, LED5.anode, Q1.C, Q2.C, Q3.C, LED19.anode
  GND: DC_Power1.GND, Arduino1.GND, P1.cathode, P2.cathode, P3.cathode, R10.Pin_1, R11.Pin_1, R12.Pin_1, R13.Pin_1, R14.Pin_1, LED7.cathode, LED11.cathode, LED12.cathode, LED13.cathode, R25.Pin_1, LED15.cathode, LED16.cathode, LED17.cathode, LED18.cathode, R26.Pin_1
  N2: Arduino1.D13, S6.leg1, R14.Pin_0
  N3: Arduino1.D12, S5.leg1, R13.Pin_0
  N4: Arduino1.D11, S4.leg1, R12.Pin_0
  N5: Arduino1.D10, S3.leg1, R11.Pin_0
  N6: Arduino1.D9, S2.leg1, R10.Pin_0
  N7: Arduino1.D7, R19.Pin_1
  N8: Arduino1.D6, R22.Pin_1
  N9: Arduino1.D5, R24.Pin_1
  N10: Arduino1.A1, R7.Pin_1, P3.anode
  N11: Arduino1.A2, R8.Pin_1, P2.anode
  N12: Arduino1.A3, R9.Pin_1, P1.anode
  N13: LED4.cathode, LED5.cathode, LED19.cathode, R26.Pin_0
  N14: Q1.E, R21.Pin_1
  N15: Q1.B, R19.Pin_0
  N16: LED7.anode, R21.Pin_0, LED15.anode, LED16.anode, LED17.anode
  N17: Q2.E, R23.Pin_1
  N18: Q2.B, R22.Pin_0
  N19: LED11.anode, LED12.anode, LED13.anode, R23.Pin_0, LED18.anode
  N20: Q3.E, SPKR2.pin1
  N21: Q3.B, R24.Pin_0
  N22: SPKR2.pin2, R25.Pin_0
